# Fritzing sketch VoltmeterDC (saved by Fritzing 0.9.3b)
breadboards: 1

parts:
  Part1 = Arduino Uno (Rev3)
  R1 = Resistor [tolerance=±5% resistance=1k package=THT]
  R2 = Resistor [tolerance=±5% resistance=1k package=THT]
  U1 = mystery part, 4 pins [chip_label=Item]
  U3 = ESP8266 WiFi Module [part_number=ESP8266]

nets:
  N1: Part1.A0, R1.Pin_1, R2.Pin_0
  N2: Part1.D0/RX, U3.TXD
  N3: Part1.D1/TX, U3.RXD
  GND: Part1.GND, R1.Pin_0, U1.pin1, U3.GND
  N4: R2.Pin_1, U1.pin4
  N5: U3.VCC, U3.CH_PD

custom parts:
  ESP8266 WiFi Module: Generic WiFi Module based on the ESP8266 with onboard PCB antenna and UART communications
